// Logisim project microprocessor.circ as structural Verilog: 14 circuits, main circuit CPU
module CPU (
);

  wire aritmaticlogicunit_1_c, aritmaticlogicunit_1_n, aritmaticlogicunit_1_o, aritmaticlogicunit_1_z, C,
       Clk, Decode, EN, Execute, Fetch, L_FSR, M_A, N, not_1_out, O, R_D, R_W_minus, SIZ, Update_PC, W_D, Z;
  wire [1:0] Func_FSR, Inst_Code;
  wire [2:0] ALU_SEL;
  wire [3:0] Mem_Addr_Reg_q, multiplexer_1_out, multiplexer_1_out_2, pc_1_output;
  wire [7:0] adder_1_out, aritmaticlogicunit_1_output, multiplexer_2_out, multiplexer_3_out, R_D_Out,
       ram_1_data, subtractor_1_out, Val_ACC, Val_FSR, Value_Given, Write_Data_Reg_q;
  wire [12:0] inst, rom_1_data;

  Multiplexer #(.select(2), .width(8), .enable("false")) multiplexer_1 (
    .in1(Value_Given), .in2(Val_FSR), .out({multiplexer_1_out_2, multiplexer_1_out}), .sel(Inst_Code));  // open: in0, in3
  // Probe on multiplexer_1_out
  // Probe on Value_Given
  // Probe on Inst_Code
  // Probe on R_D_Out
  Register #(.width(4)) Mem_Addr_Reg (.D(multiplexer_1_out), .en(M_A), .Q(Mem_Addr_Reg_q), .clk(Clk));  // open: clr
  Register Write_Data_Reg (.D(Val_ACC), .en(W_D), .Q(Write_Data_Reg_q), .clk(Clk));  // open: clr
  // Probe on Write_Data_Reg_q
  // Probe on multiplexer_2_out
  Multiplexer #(.select(2), .width(8), .enable("false")) multiplexer_2 (
    .in0(Value_Given), .in1(R_D_Out), .in2(R_D_Out), .out(multiplexer_2_out), .sel(Inst_Code));  // open: in3
  // Probe on Mem_Addr_Reg_q
  AritmaticLogicUnit aritmaticlogicunit_1 (
    .Input2(Val_ACC), .Input1(multiplexer_2_out), .C(aritmaticlogicunit_1_c),
    .Output(aritmaticlogicunit_1_output), .ALU_SEL(ALU_SEL), .Z(aritmaticlogicunit_1_z),
    .N(aritmaticlogicunit_1_n), .O(aritmaticlogicunit_1_o));
  not not_1 (not_1_out, R_W_minus);
  Flag_Regs flag_regs_1 (
    .Z(aritmaticlogicunit_1_z), .C(aritmaticlogicunit_1_c), .N(aritmaticlogicunit_1_n),
    .O(aritmaticlogicunit_1_o), .Z_Out(Z), .C_Out(C), .N_Out(N), .O_Out(O), .clk(Clk),
    .in_6({Inst_Code, ALU_SEL}), .in_7(Execute));
  // Probe on aritmaticlogicunit_1_output
  // Probe on Val_ACC
  Adder_part adder_1 (.a(8'h1), .b(Val_FSR), .out(adder_1_out));  // open: cin, cout
  Subtractor subtractor_1 (.a(Val_FSR), .b(8'h1), .out(subtractor_1_out));  // open: bin, bout
  // Probe on ram_1_data
  RAM #(.addrWidth(4), .bus("separate")) ram_1 (
    .addr(Mem_Addr_Reg_q), .din(Write_Data_Reg_q), .data(ram_1_data), .str(not_1_out), .sel(EN), .clk(Clk),
    .ld(R_W_minus));  // open: clr
  // Probe on R_D_Out
  Register Read_Data_Reg (.D(ram_1_data), .en(R_D), .Q(R_D_Out), .clk(Clk));  // open: clr
  // Probe on Val_ACC
  Register Accumulator (.D(aritmaticlogicunit_1_output), .en(Execute), .Q(Val_ACC), .clk(Clk));  // open: clr
  Multiplexer #(.select(2), .width(8), .enable("false")) multiplexer_3 (
    .in0(Value_Given), .in1(adder_1_out), .in2(subtractor_1_out), .out(multiplexer_3_out), .sel(Func_FSR));  // open: in3
  Register FSR (.D(multiplexer_3_out), .en(L_FSR), .Q(Val_FSR), .clk(Clk));  // open: clr
  PC pc_1 (.Data(Value_Given[3:0]), .Fetch(Fetch), .Output(pc_1_output), .Update_PC(Update_PC), .Clk(Clk), .SIZ(SIZ));
  ROM #(.addrWidth(4), .dataWidth(13)) rom_1 (.addr(pc_1_output), .data(rom_1_data), .sel(1'b1));
  Cont_Unit cont_unit_1 (
    .Fetch(Fetch), .Decode(Decode), .Execute(Execute), .Inst_code(Inst_Code), .R_W_minus(R_W_minus), .EN(EN),
    .M_A(M_A), .R_D(R_D), .W_D(W_D), .Value_Given(Value_Given), .Z(Z), .N(N), .Clk(Clk), .Instruction(inst),
    .ALU_SEL(ALU_SEL), .Func_FSR(Func_FSR), .SIZ(SIZ), .Update_PC(Update_PC));
  Clock u_Clk (.out(Clk));
  // Probe on rom_1_data
  // Probe on inst
  Register #(.width(13)) Instruction_Reg (.D(rom_1_data), .en(Decode), .Q(inst), .clk(Clk));  // open: clr

  // Notes on the sheet:
  //   contents of rom_1 (hex, n*v repeats v):
  //   0 402 102 1b00 1800 5 1a00 106 1903
endmodule

// ALU
module AritmaticLogicUnit (
  input  [7:0] Input1,
  input  [7:0] Input2,
  input  [2:0] ALU_SEL,
  output Z,
  output C,
  output N,
  output O,
  output [7:0] Output
);

  wire C_Add, C_Sub, O_Add, O_Sub;
  wire [7:0] add, \and , negator_1_out, \or , shiftL, shiftR, sub;

  Negator negator_1 (.in(Input1), .out(negator_1_out));
  Adder adder_1 (.input1(Input1), .input2(Input2), .Output(add), .Carry(C_Add), .Overflow(O_Add));
  Adder adder_2 (.input1(negator_1_out), .input2(Input2), .Output(sub), .Carry(C_Sub), .Overflow(O_Sub));
  assign \and  = Input1 & Input2;  // AND_Gate and, 8 bits wide
  assign \or  = Input1 | Input2;  // OR_Gate or, 8 bits wide
  Shifter shifter_1 (.in(Input1), .\dist (3'b001), .out(shiftL));
  Shifter #(.shift("lr")) shifter_2 (.in(Input1), .\dist (3'b001), .out(shiftR));
  // Probe on add
  Multiplexer #(.enable("false")) multiplexer_1 (.in0(C_Add), .in1(C_Sub), .out(C), .sel(ALU_SEL[0]));
  Multiplexer #(.enable("false")) multiplexer_2 (.in0(O_Add), .in1(O_Sub), .out(O), .sel(ALU_SEL[0]));
  // Probe on ALU_SEL
  Multiplexer #(.select(3), .width(8), .enable("false")) multiplexer_3 (
    .in0(add), .in1(sub), .in2(\and ), .in3(\or ), .in4(Input1), .in5(shiftL), .in6(shiftR), .in7({8{1'b0}}),
    .out(Output), .sel(ALU_SEL));
  Flag_Control flag_control_1 (.\input (Output), .Negative(N), .Zero(Z));

  // Other names for the same wires on the sheet: ALU_SEL_t[2:0] = ALU_SEL; is_sub = ALU_SEL[0]; mov[7:0] = Input1
endmodule

module Accumulator (
  input  [7:0] Input,
  input  Clock,
  input  Exec,
  input  AscSet0,
  output [7:0] \output 
);

  Pull_Resistor pull_resistor_1 (.node(AscSet0));
  D_Flip_Flop d_ff_1 (.clk(Clock), .D(Input[7]), .Q(\output [7]), .en(Exec), .reset(AscSet0));  // open: Qn, preset
  D_Flip_Flop d_ff_2 (.clk(Clock), .D(Input[6]), .Q(\output [6]), .en(Exec), .reset(AscSet0));  // open: Qn, preset
  D_Flip_Flop d_ff_3 (.clk(Clock), .D(Input[5]), .Q(\output [5]), .en(Exec), .reset(AscSet0));  // open: Qn, preset
  D_Flip_Flop d_ff_4 (.clk(Clock), .D(Input[4]), .Q(\output [4]), .en(Exec), .reset(AscSet0));  // open: Qn, preset
  D_Flip_Flop d_ff_5 (.clk(Clock), .D(Input[3]), .Q(\output [3]), .en(Exec), .reset(AscSet0));  // open: Qn, preset
  D_Flip_Flop d_ff_6 (.clk(Clock), .D(Input[2]), .Q(\output [2]), .en(Exec), .reset(AscSet0));  // open: Qn, preset
  D_Flip_Flop d_ff_7 (.clk(Clock), .D(Input[1]), .Q(\output [1]), .en(Exec), .reset(AscSet0));  // open: Qn, preset
  D_Flip_Flop d_ff_8 (.clk(Clock), .D(Input[0]), .Q(\output [0]), .en(Exec), .reset(AscSet0));  // open: Qn, preset

  // Other names for the same wires on the sheet: in0 = Input[0]; in1 = Input[1]; in2 = Input[2]; in3 = Input[3];
  //   in4 = Input[4]; in5 = Input[5]; in6 = Input[6]; in7 = Input[7]; out0 = \output [0]; out1 = \output [1];
  //   out2 = \output [2]; out3 = \output [3]; out4 = \output [4]; out5 = \output [5]; out6 = \output [6];
  //   out7 = \output [7]
endmodule

module Adder (
  input  [7:0] input1,
  input  [7:0] input2,
  output [7:0] Output,
  output Carry,
  output Overflow
);

  wire adder_1_cout, adder_2_cout, adder_3_cout, adder_4_cout, adder_5_cout, adder_6_cout, adder_7_cout;

  Adder_part #(.width(1)) adder_1 (.a(input1[0]), .b(input2[0]), .out(Output[0]), .cin(1'b0), .cout(adder_1_cout));
  Adder_part #(.width(1)) adder_2 (
    .a(input1[1]), .b(input2[1]), .out(Output[1]), .cin(adder_1_cout), .cout(adder_2_cout));
  Adder_part #(.width(1)) adder_3 (
    .a(input1[2]), .b(input2[2]), .out(Output[2]), .cin(adder_2_cout), .cout(adder_3_cout));
  Adder_part #(.width(1)) adder_4 (
    .a(input1[3]), .b(input2[3]), .out(Output[3]), .cin(adder_3_cout), .cout(adder_4_cout));
  Adder_part #(.width(1)) adder_5 (
    .a(input1[4]), .b(input2[4]), .out(Output[4]), .cin(adder_4_cout), .cout(adder_5_cout));
  Adder_part #(.width(1)) adder_6 (
    .a(input1[5]), .b(input2[5]), .out(Output[5]), .cin(adder_5_cout), .cout(adder_6_cout));
  Adder_part #(.width(1)) adder_7 (
    .a(input1[6]), .b(input2[6]), .out(Output[6]), .cin(adder_6_cout), .cout(adder_7_cout));
  Adder_part #(.width(1)) adder_8 (.a(input1[7]), .b(input2[7]), .out(Output[7]), .cin(adder_7_cout), .cout(Carry));
  xor xor_1 (Overflow, Carry, adder_7_cout);
endmodule

module Flag_Control (
  input  [7:0] \input ,
  output Negative,
  output Zero
);

  wire or_1_out;

  or or_1 (or_1_out, \input [0], \input [1], \input [2], \input [3], \input [4], \input [5], \input [6], \input [7]);
  not not_1 (Zero, or_1_out);

  assign Negative = \input [7];
endmodule

module Signal_Generator (
  input  [1:0] Inst_code,
  input  Z,
  input  C,
  input  N,
  input  O,
  input  [2:0] ALU_Sel,
  input  Fetch,
  input  Decode,
  input  Execute,
  input  [7:0] Value_Given,
  output W_D,
  output R_D,
  output M_A,
  output L_FSR,
  output [1:0] Func_FSR,
  output SIZ,
  output LOAD_PC
);

  wire J_Type, M_A_P, M_A_R, P_Type, R_D_P, R_D_R, R_Type, W_D_P, W_D_R;

  // R_Signal r_signal_1: pin names not known; wires that end beside it: Execute, R_Type, ALU_Sel, W_D_R, R_D_R, M_A_R
  P_Signal p_signal_1 (
    .P_Type(P_Type), .Execute(Execute), .ALU_Sel(ALU_Sel), .Value_Given(Value_Given), .W_D(W_D_P),
    .R_D(R_D_P), .M_A(M_A_P), .L_FSR(L_FSR), .Func_FSR(Func_FSR));
  Decoder #(.select(2), .enable("false")) decoder_1 (
    .out1(R_Type), .out2(P_Type), .out3(J_Type), .sel(Inst_code));  // open: out0
  J_Signal j_signal_1 (
    .Z(Z), .N(N), .J_Type(J_Type), .ALU_Sel(ALU_Sel), .Execute(Execute), .SIZ(SIZ), .LOAD_PC(LOAD_PC));
  or or_1 (W_D, W_D_P, W_D_R);
  or or_2 (R_D, R_D_P, R_D_R);
  or or_3 (M_A, M_A_P, M_A_R);

  // Notes on the sheet:
  //   0-I/1-R/2-P/3-P
endmodule

// Flags
module Flag_Regs (
  input  Z,
  input  C,
  input  N,
  input  O,
  input  clk,
  input  [4:0] in_6,
  input  in_7,
  output Z_Out,
  output C_Out,
  output N_Out,
  output O_Out
);

  wire and_1_out, and_2_out, and_3_out, and_4_out;
  wire [3:0] multiplexer_1_out;

  and and_1 (and_1_out, multiplexer_1_out[1], in_7);
  and and_2 (and_2_out, multiplexer_1_out[2], in_7);
  and and_3 (and_3_out, multiplexer_1_out[3], in_7);
  Register #(.width(1)) register_1 (.D(Z), .en(and_4_out), .Q(Z_Out), .clk(clk));  // open: clr
  and and_4 (and_4_out, multiplexer_1_out[0], in_7);
  Register #(.width(1)) register_2 (.D(C), .en(and_1_out), .Q(C_Out), .clk(clk));  // open: clr
  Register #(.width(1)) register_3 (.D(N), .en(and_2_out), .Q(N_Out), .clk(clk));  // open: clr
  Register #(.width(1)) register_4 (.D(O), .en(and_3_out), .Q(O_Out), .clk(clk));  // open: clr
  Multiplexer #(.select(5), .width(4), .enable("false")) multiplexer_1 (
    .in0(4'b1111), .in1(4'b1111), .in2(4'b1010), .in3(4'b1010), .in4(4'b1010), .in5(4'b1010), .in6(4'b1010),
    .in7(4'b0000), .in8(4'b1111), .in9(4'b1111), .in10(4'b1010), .in11(4'b1010), .in12(4'b1010),
    .in13(4'b1010), .in14(4'b1010), .in15(4'b0000), .in16(4'b0000), .in17(4'b0000), .in18(4'b0000),
    .in19(4'b0000), .in20(4'b0000), .in21(4'b0000), .in22(4'b0000), .in23(4'b0000), .in24(4'b0000),
    .in25(4'b0000), .in26(4'b0000), .in27(4'b0000), .in28(4'b0000), .in29(4'b0000), .in30(4'b0000),
    .in31(4'b0000), .out(multiplexer_1_out), .sel(in_6));

  // Other names for the same wires on the sheet: Execute = in_7
endmodule

module R_Signal (
  input  Fetch,
  input  Decode,
  input  Execute,
  input  R_Type,
  input  [2:0] ALU_Sel,
  output W_D,
  output R_D,
  output M_A
);

  wire not_1_out, STORE_out;

  and STORE (STORE_out, ALU_Sel[0], ALU_Sel[1], ALU_Sel[2]);
  not not_1 (not_1_out, W_D);
  and u_W_D (W_D, R_Type, Decode, STORE_out);
  buf u_R_D (R_D, not_1_out);  // AND_Gate
  or u_M_A (M_A, W_D, R_D);
endmodule

module P_Signal (
  input  P_Type,
  input  Execute,
  input  [2:0] ALU_Sel,
  input  [7:0] Value_Given,
  output W_D,
  output R_D,
  output M_A,
  output L_FSR,
  output [1:0] Func_FSR
);

  wire and_1_out, and_2_out, and_3_out, and_4_out, and_5_out, L_FSR_t, M_A_out, not_1_out, not_2_out,
       not_3_out, not_4_out, not_5_out, not_6_out, not_7_out, not_8_out, not_9_out, not_10_out, not_11_out,
       not_12_out, not_13_out, not_14_out, not_15_out, not_16_out, R_D_3_out, R_D_ARITHMETIC, R_D_LOAD,
       Valid, W_D_t;

  and u_Valid (Valid, P_Type, Execute);
  not not_1 (not_1_out, ALU_Sel[1]);
  not not_2 (not_2_out, ALU_Sel[0]);
  not not_3 (not_3_out, Value_Given[6]);
  not not_4 (not_4_out, Value_Given[7]);
  not not_5 (not_5_out, ALU_Sel[1]);
  not not_6 (not_6_out, ALU_Sel[0]);
  not not_7 (not_7_out, ALU_Sel[1]);
  not not_8 (not_8_out, ALU_Sel[0]);
  and u_W_D (W_D_t, Value_Given[6], Value_Given[7], ALU_Sel[2], not_1_out, not_2_out);
  and u_R_D (R_D_LOAD, not_3_out, not_4_out, ALU_Sel[2], not_5_out, not_6_out);
  and and_1 (and_1_out, ALU_Sel[2], not_7_out, not_8_out);
  not not_9 (not_9_out, and_1_out);
  not not_10 (not_10_out, and_2_out);
  and and_2 (and_2_out, ALU_Sel[2], ALU_Sel[1], ALU_Sel[0]);
  and R_D_2 (R_D_ARITHMETIC, not_9_out, not_10_out);
  not not_11 (not_11_out, Value_Given[7]);
  and and_3 (and_3_out, Value_Given[6], not_11_out, ALU_Sel[2], not_12_out, not_13_out);
  not not_12 (not_12_out, ALU_Sel[1]);
  not not_13 (not_13_out, ALU_Sel[0]);
  not not_14 (not_14_out, Value_Given[6]);
  and and_4 (and_4_out, not_14_out, Value_Given[7], ALU_Sel[2], not_15_out, not_16_out);
  not not_15 (not_15_out, ALU_Sel[1]);
  not not_16 (not_16_out, ALU_Sel[0]);
  and and_5 (and_5_out, ALU_Sel[2], ALU_Sel[1], ALU_Sel[0]);
  or u_M_A (M_A_out, W_D_t, R_D_LOAD, R_D_ARITHMETIC);
  or u_L_FSR (L_FSR_t, and_3_out, and_4_out, and_5_out);
  or R_D_3 (R_D_3_out, R_D_LOAD, R_D_ARITHMETIC);
  and and_6 (W_D, W_D_t, Valid);
  and and_7 (R_D, R_D_3_out, Valid);
  and and_8 (M_A, M_A_out, Valid);
  and and_9 (L_FSR, L_FSR_t, Valid);

  assign Func_FSR = Value_Given[7:6];

  // Other names for the same wires on the sheet: First_Two[1:0] = Value_Given[7:6]
endmodule

// J_Type
module J_Signal (
  input  J_Type,
  input  Execute,
  input  [2:0] ALU_Sel,
  input  Z,
  input  N,
  output SIZ,
  output LOAD_PC
);

  wire LOAD_PC_BIN, LOAD_PC_BIZ, LOAD_PC_BRA, LOAD_PC_SIZ, not_1_out, not_2_out, not_3_out, not_4_out,
       not_5_out, not_6_out, not_7_out, not_8_out, or_1_out, Valid;

  and and_1 (Valid, J_Type, Execute);
  not not_1 (not_1_out, ALU_Sel[1]);
  not not_2 (not_2_out, ALU_Sel[0]);
  not not_3 (not_3_out, ALU_Sel[2]);
  and BRA (LOAD_PC_BRA, not_3_out, not_1_out, not_2_out);
  not not_4 (not_4_out, ALU_Sel[0]);
  not not_5 (not_5_out, ALU_Sel[2]);
  and BIZ (LOAD_PC_BIZ, not_5_out, ALU_Sel[1], not_4_out, Z);
  not not_6 (not_6_out, ALU_Sel[2]);
  not not_7 (not_7_out, ALU_Sel[1]);
  and BIN (LOAD_PC_BIN, not_6_out, not_7_out, ALU_Sel[0], N);
  not not_8 (not_8_out, ALU_Sel[2]);
  and u_SIZ (LOAD_PC_SIZ, not_8_out, ALU_Sel[1], ALU_Sel[0], Z);
  or or_1 (or_1_out, LOAD_PC_SIZ, LOAD_PC_BIN, LOAD_PC_BRA, LOAD_PC_BIZ);
  and and_2 (SIZ, Valid, LOAD_PC_SIZ);
  and and_3 (LOAD_PC, Valid, or_1_out);
endmodule

// State_Machine
module State_Machine2 (
  input  LOAD,
  input  STORE,
  input  JUMP,
  input  Clk,
  output [8:0] STATE
);

  wire and_3_out, Branch2, Decode, Execute, not_1_out, not_2_out, not_3_out, or_1_out, or_4_out,
       Read_Execute, START, Store_Execute;

  or or_1 (or_1_out, Store_Execute, Execute, Branch2);
  or or_2 (STATE[0], or_1_out, START);
  and and_1 (STATE[3], Decode, LOAD);
  and and_2 (STATE[5], Decode, STORE);
  not not_1 (not_1_out, LOAD);
  not not_2 (not_2_out, JUMP);
  not not_3 (not_3_out, STORE);
  and and_3 (and_3_out, Decode, not_1_out, not_3_out, not_2_out);
  or or_3 (STATE[2], and_3_out, Read_Execute);
  and and_4 (STATE[7], Decode, JUMP);
  Register #(.width(9)) register_1 (
    .D(STATE), .en(1'b1),
    .Q({Branch2, STATE[8], Read_Execute, STATE[4], Store_Execute, STATE[6], Execute, Decode, STATE[1]}),
    .clk(Clk));  // open: clr
  not not_4 (START, or_4_out);
  or or_4 (or_4_out, STATE[1], Decode, Execute, STATE[6], Store_Execute, STATE[4], Read_Execute, STATE[8], Branch2);

  // Other names for the same wires on the sheet: Decode_Out = STATE[1]; Fetch = STATE[1]; Read_Execute_Out = STATE[6];
  //   Read_Mem = STATE[6]; Store_Execute_Out = STATE[4]; Write_Mem = STATE[4]; Branch = STATE[8];
  //   Branch2_Out = STATE[8]; Fetch_Out = STATE[0]; Execute_Out = STATE[2]; Read_Mem_Out = STATE[3];
  //   Write_Mem_Out = STATE[5]; Branch_Out = STATE[7]
endmodule

// Combinational Circuit
module Comb_Circ (
  input  [8:0] STATE,
  input  Z,
  input  N,
  input  [2:0] ALU_Sel,
  output Fetch,
  output Decode,
  output SIZ,
  output Execute,
  output Update_PC,
  output R_W_minus,
  output EN,
  output M_A,
  output R_D,
  output W_D
);

  wire and_3_out, and_4_out, Disable, not_2_out, not_3_out, not_4_out, not_5_out, OP_BIN, OP_BIZ, OP_BRA,
       OP_CALL, OP_RETURN, OP_SIZ, or_2_out, or_3_out, or_4_out, or_5_out;

  or or_1 (Disable, STATE[0], STATE[1]);
  or or_2 (or_2_out, STATE[4], STATE[5]);
  not not_1 (R_W_minus, or_2_out);
  or or_3 (or_3_out, STATE[6], STATE[4]);
  not not_2 (not_2_out, Disable);
  and and_1 (EN, not_2_out, or_3_out);
  Decoder #(.select(3), .enable("false")) decoder_1 (
    .out0(OP_BRA), .out1(OP_BIN), .out2(OP_BIZ), .out3(OP_SIZ), .out4(OP_CALL), .out5(OP_RETURN),
    .sel(ALU_Sel));  // open: out6, out7
  or or_4 (or_4_out, STATE[3], STATE[5]);
  not not_3 (not_3_out, Disable);
  and and_2 (M_A, not_3_out, or_4_out);
  and and_3 (and_3_out, OP_BIN, N);
  and and_4 (and_4_out, OP_BIZ, Z);
  and and_5 (SIZ, OP_SIZ, Z);
  not not_4 (not_4_out, Disable);
  and and_6 (R_D, not_4_out, STATE[6]);
  or or_5 (or_5_out, OP_BRA, and_3_out, and_4_out, SIZ);
  and and_7 (Update_PC, or_5_out, STATE[7]);
  not not_5 (not_5_out, Disable);
  and and_8 (W_D, not_5_out, STATE[5]);

  assign Decode = STATE[1];
  assign Execute = STATE[2];
  assign Fetch = STATE[0];

  // Other names for the same wires on the sheet: Read_Mem = STATE[3]; Store_Execute = STATE[4]; Write_Mem = STATE[5];
  //   Read_Execute = STATE[6]; Branch = STATE[7]
endmodule

// Control Unit
module Cont_Unit (
  input  Z,
  input  N,
  input  [12:0] Instruction,
  input  Clk,
  output SIZ,
  output Update_PC,
  output Fetch,
  output R_W_minus,
  output Decode,
  output EN,
  output Execute,
  output M_A,
  output [1:0] Inst_code,
  output R_D,
  output W_D,
  output [2:0] ALU_SEL,
  output [1:0] Func_FSR,
  output [7:0] Value_Given
);

  wire and_3_out, and_4_out, and_5_out, and_6_out, JUMP, LOAD, not_1_out, not_2_out, not_3_out, STORE;
  wire [8:0] STATE;

  State_Machine2 state_machine2_1 (.STATE(STATE), .LOAD(LOAD), .STORE(STORE), .Clk(Clk), .JUMP(JUMP));
  // Probe on Instruction[12:11]
  Comb_Circ comb_circ_1 (
    .Fetch(Fetch), .Decode(Decode), .Execute(Execute), .STATE(STATE), .Z(Z), .N(N),
    .ALU_Sel(Instruction[10:8]), .SIZ(SIZ), .Update_PC(Update_PC), .R_W_minus(R_W_minus), .EN(EN), .M_A(M_A),
    .R_D(R_D), .W_D(W_D));
  and and_1 (STORE, and_3_out, and_4_out);
  and and_2 (LOAD, and_5_out, not_1_out);
  not not_1 (not_1_out, and_6_out);
  and and_3 (and_3_out, Instruction[11], not_2_out);
  not not_2 (not_2_out, Instruction[12]);
  and and_4 (and_4_out, Instruction[8], Instruction[9], Instruction[10]);
  not not_3 (not_3_out, Instruction[12]);
  and and_5 (and_5_out, Instruction[11], not_3_out);
  and and_6 (and_6_out, Instruction[8], Instruction[9], Instruction[10]);
  and and_7 (JUMP, Instruction[11], Instruction[12]);

  assign ALU_SEL = Instruction[10:8];
  assign Inst_code = Instruction[12:11];
  assign Value_Given = Instruction[7:0];
endmodule

module PC (
  input  SIZ,
  input  Update_PC,
  input  [3:0] Data,
  input  Fetch,
  input  Clk,
  output [3:0] Output
);

  wire [3:0] adder_1_out, multiplexer_1_out, subtractor_1_out;

  Multiplexer #(.width(4), .enable("false")) multiplexer_1 (
    .in0(Data), .in1(adder_1_out), .out(multiplexer_1_out), .sel(SIZ));
  Subtractor #(.width(4)) subtractor_1 (.a(multiplexer_1_out), .b(4'b0001), .out(subtractor_1_out));  // open: bin, bout
  Counter #(.width(4), .max('hf)) PC (
    .load(Update_PC), .D(subtractor_1_out), .count(Fetch), .Q(Output), .clk(Clk));  // open: carry, clr
  Adder_part #(.width(4)) adder_1 (.a(Output), .b(4'b0010), .out(adder_1_out));  // open: cin, cout
endmodule
